// Logisim project одв3-8.circ as structural Verilog: 1 circuit, main circuit main
// A
module main (
  input  A,
  input  in_2,
  input  in_3,
  input  in_4,
  input  in_5,
  input  in_6,
  input  in_7,
  input  in_8,
  input  B,
  input  in_10,
  input  in_11,
  input  in_12,
  input  in_13,
  input  in_14,
  input  in_15,
  input  in_16,
  output d,
  output out_18,
  output out_19,
  output out_20,
  output out_21,
  output out_22,
  output out_23,
  output out_24
);

  wire and_1_out, and_2_out, and_3_out, and_4_out, and_5_out, and_6_out, and_7_out, and_8_out, and_9_out,
       and_10_out, and_11_out, and_12_out, and_13_out, and_14_out, and_15_out, and_16_out, and_17_out,
       and_18_out, and_19_out, and_20_out, and_21_out, and_22_out, and_23_out, and_24_out, and_25_out,
       and_26_out, and_27_out, and_28_out, and_29_out, and_30_out, and_31_out, and_32_out, and_33_out,
       and_34_out, and_35_out, and_36_out, and_37_out, and_38_out, and_39_out, and_40_out, not_1_out,
       not_2_out, not_3_out, not_4_out, not_5_out, not_6_out, not_7_out, not_8_out, not_9_out, not_10_out,
       not_11_out, not_12_out, not_13_out, not_14_out, not_15_out, not_16_out, not_17_out, not_18_out,
       not_19_out, not_20_out, not_21_out, not_22_out, not_23_out, not_24_out, or_1_out, or_2_out, or_3_out,
       or_5_out, or_6_out, or_7_out, or_9_out, or_10_out, or_11_out, or_13_out, or_14_out, or_15_out,
       or_17_out, or_18_out, or_19_out, or_21_out, or_22_out, or_23_out, or_25_out, or_26_out, or_27_out,
       or_29_out, or_30_out, or_31_out;

  not not_1 (not_1_out, B);
  not not_2 (not_2_out, A);
  not not_3 (not_3_out, or_7_out);
  and and_1 (and_1_out, not_2_out, or_7_out, not_1_out);
  and and_2 (and_2_out, not_2_out, B, not_3_out);
  and and_3 (and_3_out, or_7_out, B, A);
  and and_4 (and_4_out, not_2_out, B, or_7_out);
  and and_5 (and_5_out, A, not_1_out, not_3_out);
  LED led_1 (.in(or_3_out));
  or or_1 (or_1_out, and_1_out, and_2_out);
  or or_2 (or_2_out, or_1_out, and_3_out);
  or or_3 (or_3_out, or_2_out, and_4_out);
  or or_4 (d, or_2_out, and_5_out);
  not not_4 (not_4_out, in_2);
  not not_5 (not_5_out, in_10);
  not not_6 (not_6_out, or_11_out);
  and and_6 (and_6_out, not_4_out, or_11_out, not_5_out);
  and and_7 (and_7_out, not_4_out, in_10, not_6_out);
  and and_8 (and_8_out, or_11_out, in_10, in_2);
  and and_9 (and_9_out, not_4_out, in_10, or_11_out);
  and and_10 (and_10_out, in_2, not_5_out, not_6_out);
  or or_5 (or_5_out, and_6_out, and_7_out);
  or or_6 (or_6_out, or_5_out, and_8_out);
  or or_7 (or_7_out, or_6_out, and_9_out);
  or or_8 (out_18, or_6_out, and_10_out);
  not not_7 (not_7_out, in_3);
  not not_8 (not_8_out, in_11);
  not not_9 (not_9_out, or_15_out);
  and and_11 (and_11_out, not_7_out, or_15_out, not_8_out);
  and and_12 (and_12_out, not_7_out, in_11, not_9_out);
  and and_13 (and_13_out, or_15_out, in_11, in_3);
  and and_14 (and_14_out, not_7_out, in_11, or_15_out);
  and and_15 (and_15_out, in_3, not_8_out, not_9_out);
  or or_9 (or_9_out, and_11_out, and_12_out);
  or or_10 (or_10_out, or_9_out, and_13_out);
  or or_11 (or_11_out, or_10_out, and_14_out);
  or or_12 (out_19, or_10_out, and_15_out);
  not not_10 (not_10_out, in_4);
  not not_11 (not_11_out, in_12);
  not not_12 (not_12_out, or_19_out);
  and and_16 (and_16_out, not_10_out, or_19_out, not_11_out);
  and and_17 (and_17_out, not_10_out, in_12, not_12_out);
  and and_18 (and_18_out, or_19_out, in_12, in_4);
  and and_19 (and_19_out, not_10_out, in_12, or_19_out);
  and and_20 (and_20_out, in_4, not_11_out, not_12_out);
  or or_13 (or_13_out, and_16_out, and_17_out);
  or or_14 (or_14_out, or_13_out, and_18_out);
  or or_15 (or_15_out, or_14_out, and_19_out);
  or or_16 (out_20, or_14_out, and_20_out);
  not not_13 (not_13_out, in_5);
  not not_14 (not_14_out, in_13);
  not not_15 (not_15_out, or_23_out);
  and and_21 (and_21_out, not_13_out, or_23_out, not_14_out);
  or or_17 (or_17_out, and_21_out, and_22_out);
  and and_22 (and_22_out, not_13_out, in_13, not_15_out);
  and and_23 (and_23_out, or_23_out, in_13, in_5);
  and and_24 (and_24_out, not_13_out, in_13, or_23_out);
  and and_25 (and_25_out, in_5, not_14_out, not_15_out);
  or or_18 (or_18_out, or_17_out, and_23_out);
  or or_19 (or_19_out, or_18_out, and_24_out);
  or or_20 (out_21, or_18_out, and_25_out);
  not not_16 (not_16_out, in_6);
  not not_17 (not_17_out, in_14);
  not not_18 (not_18_out, or_27_out);
  and and_26 (and_26_out, not_16_out, or_27_out, not_17_out);
  and and_27 (and_27_out, not_16_out, in_14, not_18_out);
  and and_28 (and_28_out, or_27_out, in_14, in_6);
  and and_29 (and_29_out, not_16_out, in_14, or_27_out);
  and and_30 (and_30_out, in_6, not_17_out, not_18_out);
  or or_21 (or_21_out, and_26_out, and_27_out);
  or or_22 (or_22_out, or_21_out, and_28_out);
  or or_23 (or_23_out, or_22_out, and_29_out);
  or or_24 (out_22, or_22_out, and_30_out);
  not not_19 (not_19_out, in_7);
  not not_20 (not_20_out, in_15);
  not not_21 (not_21_out, or_31_out);
  and and_31 (and_31_out, not_19_out, or_31_out, not_20_out);
  and and_32 (and_32_out, not_19_out, in_15, not_21_out);
  and and_33 (and_33_out, or_31_out, in_15, in_7);
  and and_34 (and_34_out, not_19_out, in_15, or_31_out);
  and and_35 (and_35_out, in_7, not_20_out, not_21_out);
  or or_25 (or_25_out, and_31_out, and_32_out);
  or or_26 (or_26_out, or_25_out, and_33_out);
  or or_27 (or_27_out, or_26_out, and_34_out);
  or or_28 (out_23, or_26_out, and_35_out);
  not not_22 (not_22_out, in_8);
  not not_23 (not_23_out, in_16);
  not not_24 (not_24_out, 1'b0);
  and and_36 (and_36_out, not_22_out, 1'b0, not_23_out);
  or or_29 (or_29_out, and_36_out, and_37_out);
  and and_37 (and_37_out, not_22_out, in_16, not_24_out);
  and and_38 (and_38_out, 1'b0, in_16, in_8);
  and and_39 (and_39_out, not_22_out, in_16, 1'b0);
  and and_40 (and_40_out, in_8, not_23_out, not_24_out);
  or or_30 (or_30_out, or_29_out, and_38_out);
  or or_31 (or_31_out, or_30_out, and_39_out);
  or or_32 (out_24, or_30_out, and_40_out);

  // Notes on the sheet:
  //   Х1
  //   Х2
  //   Х3
  //   b*
  //   b
  //   d
  //   Х1
  //   Х2
  //   Х3
  //   b*
  //   b
  //   d
  //   Х1
  //   Х2
  //   Х3
  //   b*
  //   b
  //   Х1
  //   Х2
  //   Х3
  //   b*
  //   b
  //   d
  //   Х1
  //   Х2
  //   Х3
  //   b*
  //   b
  //   d
  //   Х1
  //   Х2
  //   Х3
  //   b*
  //   b
  //   d
  //   Х1
  //   Х3
  //   Х2
  //   b*
  //   b
  //   d
  //   Х1
  //   Х2
  //   Х3
  //   b*
  //   b
endmodule
